# Fritzing sketch gioco delle giostre (saved by Fritzing 0.9.3b)

parts:
  BAT1 = 18650 battery holder [package=battery-18650-kit]
  BAT2 = 18650 battery holder [package=battery-18650-kit]
  U1_impostato_4_5_volt = LM2596 step down module
  Componente1 = Arduino Nano (Rev3.0)
  S1 = Pushbutton [package="[THT]"]
  S2 = Pushbutton [package="[THT]"]
  S3 = Pushbutton [package="[THT]"]
  R1 = Resistor [tolerance=±5% resistance=100k package=THT]
  R2 = Resistor [tolerance=±5% resistance=100k package=THT]
  R3 = Resistor [tolerance=±5% resistance=100k package=THT]
  Q1 = NPN-Transistor [package="TO92 [THT]"]
  Q2 = NPN-Transistor [package="TO92 [THT]"]
  Q3 = NPN-Transistor [package="TO92 [THT]"]
  Q4 = NPN-Transistor [package="TO92 [THT]"]
  Q5 = NPN-Transistor [package="TO92 [THT]"]
  Q6 = NPN-Transistor [package="TO92 [THT]"]
  R4 = Resistor [tolerance=±5% resistance=1k package=THT]
  R5 = Resistor [tolerance=±5% resistance=1k package=THT]
  R6 = Resistor [tolerance=±5% resistance=1k package=THT]
  R7 = Resistor [tolerance=±5% resistance=1k package=THT]
  R8 = Resistor [tolerance=±5% resistance=1k package=THT]
  R9 = Resistor [tolerance=±5% resistance=1k package=THT]
  R10 = Resistor [tolerance=±5% resistance=100k package=THT]
  R11 = Resistor [tolerance=±5% resistance=100k package=THT]
  R12 = Resistor [tolerance=±5% resistance=100k package=THT]
  R13 = Resistor [tolerance=±5% resistance=100k package=THT]
  R14 = Resistor [tolerance=±5% resistance=100k package=THT]
  R15 = Resistor [tolerance=±5% resistance=100k package=THT]
  M1 = DC Motor
  J1 = Piezo Speaker
  J2 = Piezo Speaker
  J3 = Piezo Speaker
  M2 = DC Motor
  M3 = DC Motor

nets:
  N1: BAT1.+, BAT2.-
  N2: BAT1.-, U1_impostato_4_5_volt.IN-, U1_impostato_4_5_volt.OUT-, Componente1.RESET, M1.pin_1, J1.pin1, J2.pin1, J3.pin1, M2.pin_1, M3.pin_1
  N3: BAT2.+, U1_impostato_4_5_volt.IN+, Componente1.VIN
  N4: U1_impostato_4_5_volt.OUT+, Q1.C, Q2.C, Q3.C, Q4.C, Q5.C, Q6.C
  N5: Componente1.GND, S1.Pin_1, S1.Pin_2, S2.Pin_1, S2.Pin_2, S3.Pin_2, R10.Pin_1, R11.Pin_0, R12.Pin_1, R13.Pin_1, R14.Pin_1, R15.Pin_1
  N6: Componente1.D7, R4.Pin_1
  N7: Componente1.D8, R5.Pin_1
  N8: Componente1.D9, R6.Pin_1
  N9: Componente1.D10, R7.Pin_1
  N10: Componente1.D11/MOSI, R8.Pin_1
  N11: Componente1.D12/MISO, R9.Pin_1
  N12: Componente1.5V, R1.Pin_1, R2.Pin_1, R3.Pin_1
  N13: Componente1.A2, S3.Pin_3, S3.Pin_4, R3.Pin_0
  N14: Componente1.A1, S2.Pin_3, S2.Pin_4, R2.Pin_0
  N15: Componente1.A0, S1.Pin_3, S1.Pin_4, R1.Pin_0
  N16: Q1.E, M1.pin_2
  N17: Q1.B, R4.Pin_0, R10.Pin_0
  N18: Q2.E, J1.pin2
  N19: Q2.B, R5.Pin_0, R11.Pin_1
  N20: Q3.E, M2.pin_2
  N21: Q3.B, R6.Pin_0, R12.Pin_0
  N22: Q4.E, J2.pin2
  N23: Q4.B, R7.Pin_0, R13.Pin_0
  N24: Q5.E, M3.pin_2
  N25: Q5.B, R8.Pin_0, R14.Pin_0
  N26: Q6.E, J3.pin2
  N27: Q6.B, R9.Pin_0, R15.Pin_0

custom parts:
  18650 battery holder: 18650 Battery Holder
  LM2596 step down module: LM2596 DC-DC step down power supply module 3 A.
